# Fritzing sketch Breadboard Layout (saved by Fritzing 0.9.6b)
circuit board: 6.89435cm x 5.47652cm
breadboards: 1

parts:
  ESP32 = ESP32S-HiLetgo [part_number=ESP32]
  Pair_button = Pushbutton [package="[THT]"]
  Pair_LED = LED - 5mm [color="Red (633nm)" current=0.030 package="5 mm [THT]"]
  Door-signal = LED - 5mm [color="Green (560nm)" current=0.030 package="5 mm [THT]"]
  R1 = Resistor [tolerance=±5% power=0.25 resistance=220 package=THT]

nets:
  N1: ESP32.GPIO32, Pair_LED.anode
  N2: ESP32.GPIO27, Pair_button.Pin_1, Pair_button.Pin_2, Pair_button.Pin_3, Pair_button.Pin_4, Pair_LED.cathode, Door-signal.cathode, R1.Pin_0
  N3: ESP32.GND, R1.Pin_1
  N4: ESP32.GPIO5, Door-signal.anode

notes:
  #LowEffortKandidat

custom parts:
  ESP32S-HiLetgo: HiLetgo ESP-WROOM-32 ESP32 ESP-32S Development Board 2.4GHz Dual-Mode WiFi + Bluetooth Dual Cores Microcontroller The ESP32 integrated with Antenna switches, RF Balun, power amplifiers, low-noise amplifiers, filters, and management modules, and the entire solution occupies the least area of PCB. 2.4 GHz Wi-Fi plus Bluetooth dual-mode chip, with TSMC Ultra-low power consumption 40nm technology,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
